# Fritzing sketch GROUPEFREE (saved by Fritzing 0.9.3b)
breadboards: 1

parts:
  relais = Arduino BT
  DHT12 = DHT11 Humitidy and Temperature Sensor
  Capacitive_Soil_Moisture_Sensor1 = Capacitive Soil Moisture Sensor V2.0
  WATER_PUMP1 = water pump/motor
  M1 = 1 chan 5v relay module
  F1 = Fan - Ventilador [package=THT]
  BAT1 = BC9VPC [package=bc9vpc]
  BAT2 = BC9VPC [package=bc9vpc]
  M2 = 1 chan 5v relay module

nets:
  N1: relais.D8, M1.pin_3
  N2: relais.A1, Capacitive_Soil_Moisture_Sensor1.AOUT
  N3: relais.D2, DHT12.DATA
  N4: relais.D4, M2.pin_3
  GND: relais.GND, DHT12.GND, Capacitive_Soil_Moisture_Sensor1.GND, M2.pin_2
  5V: relais.5V, DHT12.VDD, Capacitive_Soil_Moisture_Sensor1.VCC, M1.pin_1, M2.pin_1
  N5: WATER_PUMP1.pin_1, BAT1.V-
  N6: WATER_PUMP1.pin_2, M1.pin_5
  N7: M1.pin_4, BAT1.V+
  N8: F1.5V, M2.pin_5
  N9: F1.GND, BAT2.V-
  N10: BAT2.V+, M2.pin_4

custom parts:
  DHT11 Humitidy and Temperature Sensor: DHT11 Humidity and Temperature Sensor
  water pump/motor: WATER PUMP BY ARDUBLOCKTR
  1 chan 5v relay module: 1 Channel 5V Relay Module Board Shield with Optocoupler Support High and Low Level Trigger for Arduino.
  Fan - Ventilador: Ventilador de 2 pines, se encuentra comunmente en computadoras de escritorio

// code stored in the sketch: Untitled2.ino
file:///C:/Users/solutions tech/Downloads/DHT11 Humitidy and Temperature Sensor (1).fzpz
file:///C:/Users/solutions tech/Downloads/DHT11 Humitidy and Temperature Sensor (1).fzpz
/*tout d'abord je declare mes variables 
ainsi que les broche qui seront utilise
sur la carte arduino/**/

int val;
int capteur_de_sol=A1;/*pour dire que le capteur de sol 
sera connecter a la broche numero 3 de la carte*/

int relai_pompe=8;/*pour dire que le relais relier a la pompe
sera connecter a la broche numero 7 de la carte*/

void setup() {
  
Serial.begin(9600);/*pour initialiser le moniteur serie
afin de visualise les donnee
qui seront recolte par le capteur */

pinMode(capteur_de_sol,INPUT);/*pour dire que la
broche du capteur aura pour fontion de faire entree
le courant de la broche 3*/

pinMode(relai_pompe,OUTPUT);/*pour dire que la
broche du relais relier a la pompe aura pour fontion de faire sorti
le courant de la broche 7*/
}

void loop() {
  
val=analogRead(capteur_de_sol);/*pour recevoire les valeur
du capteur dans la broche 3 et le stocke dans une varable <<val>>*/

Serial.println(val);/*pour afficher les donnee recu
du capteur dans le moniteur serie */

if(val>=200){

digitalWrite(relai_pompe,HIGH);/*pour fait sorti le courant
dans la broche 7 afin d'activer le relai*/

} else {

digitalWrite(relai_pompe,LOW);/*pour fait sorti le courant
dans la broche 7 afin d'activer le relai*/ }

}
